// Logisim project Meow.circ as structural Verilog: 1 circuit, main circuit main
// 1
module main (
);

  wire cdm16_1_p1, cdm16_1_p2, cdm16_1_p3, cdm16_1_p5, cdm16_1_p6, cdm16_1_p7, cdm16_1_p8, cdm16_1_p9,
       cdm16_1_p10, clock, mem, not_1_out, read, select, uart_1_p6, word;
  wire [15:0] address_bus, cdm16_1_p15, cdm16_1_p16, data_bus;

  // Debugger debugger_1: pin names not known
  // Probe on cdm16_1_p3
  // Probe on cdm16_1_p2
  // Probe on cdm16_1_p5
  // Probe on cdm16_1_p6
  // cdm16 cdm16_1: pin names not known; wires that end beside it: cdm16_1_p1, cdm16_1_p2, cdm16_1_p3, clock, cdm16_1_p5, cdm16_1_p6, cdm16_1_p7, cdm16_1_p8, cdm16_1_p9, cdm16_1_p10, mem, read, word, address_bus, cdm16_1_p15, cdm16_1_p16
  Clock clock_1 (.out(clock));
  // Probe on cdm16_1_p8
  // Probe on cdm16_1_p7
  Comparator #(.width(15)) comparator_1 (.a(address_bus[14:0]), .b(15'h7f80), .eq(select));  // open: gt, lt
  // Probe on cdm16_1_p9
  // Probe on cdm16_1_p10
  assign cdm16_1_p16 = read ? data_bus : 16'bz;  // Controlled_Buffer controlled_buffer_1
  assign data_bus = not_1_out ? cdm16_1_p15 : 16'bz;  // Controlled_Buffer controlled_buffer_2
  not not_1 (not_1_out, read);
  // UART uart_1: pin names not known; wires that end beside it: cdm16_1_p15[7:0], cdm16_1_p16[7:0], cdm16_1_p1, clock, read, uart_1_p6
  // RAM ram_1: pin names not known; wires that end beside it: address_bus, word, mem, clock, read, data_bus
  and and_1 (uart_1_p6, select, mem);
endmodule
